// Logisim project Reconfigurable Multiplier.circ as structural Verilog: 5 circuits, main circuit main
module main (
  input  [14:0] Multiplier,
  input  [14:0] Multiplicand,
  input  Yi,
  input  Yi_1,
  input  Multiplier_Bits,
  input  in_6,
  input  in_7,
  input  Multiplier_2,
  input  Yi_2,
  input  Yi_1_2,
  input  in_11,
  input  in_12,
  input  in_13,
  input  Yi_3,
  input  Yi_1_3,
  input  in_16,
  input  in_17,
  input  in_18,
  input  Yi_4,
  input  Yi_1_4,
  input  in_21,
  input  in_22,
  input  in_23,
  input  Yi_5,
  input  Yi_1_5,
  input  in_26,
  input  in_27,
  input  in_28,
  input  Yi_6,
  input  Yi_1_6,
  input  in_31,
  input  in_32,
  input  in_33,
  input  Yi_7,
  input  Yi_1_7,
  input  in_36,
  input  in_37,
  input  in_38,
  input  Yi_8,
  input  Yi_1_8,
  input  in_41,
  input  in_42,
  input  in_43
);

  wire booth_encoder_2_neg, booth_encoder_2_one, booth_encoder_2_two, booth_encoder_6_neg,
       booth_encoder_6_one, booth_encoder_6_two, booth_encoder_7_neg, booth_encoder_7_one,
       booth_encoder_7_two, booth_encoder_8_neg, booth_encoder_8_one, booth_encoder_8_two,
       control_circuit_1_out_5, control_circuit_1_out_6, control_circuit_1_out_7, control_circuit_1_out_8,
       control_circuit_1_out_10, control_circuit_1_out_11, control_circuit_1_out_12,
       control_circuit_1_out_13, control_circuit_1_out_14, control_circuit_1_out_15,
       control_circuit_1_out_16, control_circuit_1_out_17, control_circuit_1_out_18,
       control_circuit_1_out_19, control_circuit_1_out_20, n1_bit_multiplier_block_2_out_5,
       n1_bit_multiplier_block_3_out_5, n1_bit_multiplier_block_3_out_6, n1_bit_multiplier_block_4_out_5,
       n1_bit_multiplier_block_5_out_5, n1_bit_multiplier_block_5_out_6, n1_bit_multiplier_block_6_out_5,
       n1_bit_multiplier_block_6_out_6, n1_bit_multiplier_block_7_out_5, n1_bit_multiplier_block_7_out_6,
       n1_bit_multiplier_block_8_out_5, n1_bit_multiplier_block_9_out_5, n1_bit_multiplier_block_9_out_6,
       n1_bit_multiplier_block_10_out_5, n1_bit_multiplier_block_10_out_6, n1_bit_multiplier_block_11_out_5,
       n1_bit_multiplier_block_11_out_6, n1_bit_multiplier_block_12_out_5, n1_bit_multiplier_block_12_out_6,
       n1_bit_multiplier_block_13_p1, n1_bit_multiplier_block_13_p2, n1_bit_multiplier_block_13_p4,
       n1_bit_multiplier_block_14_out_5, n1_bit_multiplier_block_14_out_6, n1_bit_multiplier_block_15_out_5,
       n1_bit_multiplier_block_15_out_6, n1_bit_multiplier_block_16_out_5, n1_bit_multiplier_block_16_out_6,
       n1_bit_multiplier_block_17_out_5, n1_bit_multiplier_block_17_out_6, n1_bit_multiplier_block_19_out_5,
       n1_bit_multiplier_block_19_out_6, n1_bit_multiplier_block_20_out_5, n1_bit_multiplier_block_20_out_6,
       n1_bit_multiplier_block_21_out_5, n1_bit_multiplier_block_21_out_6, n1_bit_multiplier_block_22_p1,
       n1_bit_multiplier_block_22_p2, n1_bit_multiplier_block_22_p3, n1_bit_multiplier_block_22_p4,
       n1_bit_multiplier_block_22_p5, n1_bit_multiplier_block_23_out_6, n1_bit_multiplier_block_24_out_5,
       n1_bit_multiplier_block_24_out_6, n1_bit_multiplier_block_25_out_5, n1_bit_multiplier_block_25_out_6,
       n1_bit_multiplier_block_26_out_5, n1_bit_multiplier_block_26_out_6, n1_bit_multiplier_block_27_p1,
       n1_bit_multiplier_block_27_p3, n1_bit_multiplier_block_27_p4, n1_bit_multiplier_block_28_out_6,
       n1_bit_multiplier_block_29_p1, n1_bit_multiplier_block_29_p2, n1_bit_multiplier_block_29_p3,
       n1_bit_multiplier_block_29_p4, n1_bit_multiplier_block_29_p5, n1_bit_multiplier_block_30_out_6,
       n1_bit_multiplier_block_31_out_5, n1_bit_multiplier_block_31_out_6, n1_bit_multiplier_block_32_out_5,
       n1_bit_multiplier_block_33_out_5, n1_bit_multiplier_block_34_out_6, n1_bit_multiplier_block_35_out_5,
       n1_bit_multiplier_block_35_out_6, n1_bit_multiplier_block_36_out_5, n1_bit_multiplier_block_36_out_6,
       n1_bit_multiplier_block_37_out_5, n1_bit_multiplier_block_37_out_6, n1_bit_multiplier_block_38_out_5,
       n1_bit_multiplier_block_39_out_5, n1_bit_multiplier_block_39_out_6, n1_bit_multiplier_block_40_out_6,
       n1_bit_multiplier_block_41_out_5, n1_bit_multiplier_block_41_out_6, n1_bit_multiplier_block_42_out_6,
       n1_bit_multiplier_block_43_out_5, n1_bit_multiplier_block_43_out_6, n1_bit_multiplier_block_45_out_5,
       n1_bit_multiplier_block_45_out_6, n1_bit_multiplier_block_46_out_5, n1_bit_multiplier_block_46_out_6,
       n1_bit_multiplier_block_47_out_6, n1_bit_multiplier_block_48_out_5, n1_bit_multiplier_block_48_out_6,
       n1_bit_multiplier_block_49_out_5, n1_bit_multiplier_block_49_out_6, n1_bit_multiplier_block_50_out_5,
       n1_bit_multiplier_block_50_out_6, n1_bit_multiplier_block_51_out_6, n1_bit_multiplier_block_52_out_5,
       n1_bit_multiplier_block_52_out_6, n1_bit_multiplier_block_54_out_5, n1_bit_multiplier_block_54_out_6,
       n1_bit_multiplier_block_55_out_6, n1_bit_multiplier_block_56_out_5, n1_bit_multiplier_block_56_out_6,
       n1_bit_multiplier_block_57_out_5, n1_bit_multiplier_block_57_out_6, n1_bit_multiplier_block_58_out_5,
       n1_bit_multiplier_block_58_out_6, n1_bit_multiplier_block_60_out_5, n1_bit_multiplier_block_60_out_6,
       n1_bit_multiplier_block_61_out_5, n1_bit_multiplier_block_61_out_6, n1_bit_multiplier_block_62_out_6,
       n1_bit_multiplier_block_63_out_5, n1_bit_multiplier_block_63_out_6, n1_bit_multiplier_block_64_out_5,
       n1_bit_multiplier_block_64_out_6, n1_bit_multiplier_block_65_out_5, n1_bit_multiplier_block_65_out_6,
       n1_bit_multiplier_block_66_out_6, n1_bit_multiplier_block_67_out_6, n1_bit_multiplier_block_68_out_5,
       n1_bit_multiplier_block_68_out_6, n1_bit_multiplier_block_69_out_6, n1_bit_multiplier_block_70_out_6,
       n1_bit_multiplier_block_71_p1, n1_bit_multiplier_block_71_p2, n1_bit_multiplier_block_71_p3,
       n1_bit_multiplier_block_71_p4, n1_bit_multiplier_block_71_p5, n1_bit_multiplier_block_72_out_5,
       n1_bit_multiplier_block_72_out_6, n1_bit_multiplier_block_73_out_6, n1_bit_multiplier_block_74_out_6,
       n1_bit_multiplier_block_75_out_5, n1_bit_multiplier_block_75_out_6, n1_bit_multiplier_block_76_out_5,
       n1_bit_multiplier_block_76_out_6, n1_bit_multiplier_block_77_out_6, n1_bit_multiplier_block_78_out_5,
       n1_bit_multiplier_block_79_out_5, n1_bit_multiplier_block_79_out_6, n1_bit_multiplier_block_80_out_6,
       n1_bit_multiplier_block_82_out_6, n1_bit_multiplier_block_83_out_5, n1_bit_multiplier_block_83_out_6,
       n1_bit_multiplier_block_84_out_5, n1_bit_multiplier_block_84_out_6, n1_bit_multiplier_block_85_out_6,
       n1_bit_multiplier_block_86_out_5, n1_bit_multiplier_block_86_out_6, n1_bit_multiplier_block_87_out_6,
       n1_bit_multiplier_block_88_out_6, n1_bit_multiplier_block_89_out_5, n1_bit_multiplier_block_89_out_6,
       n1_bit_multiplier_block_90_out_5, n1_bit_multiplier_block_90_out_6, n1_bit_multiplier_block_91_out_6,
       n1_bit_multiplier_block_92_out_5, n1_bit_multiplier_block_92_out_6, n1_bit_multiplier_block_94_out_6,
       n1_bit_multiplier_block_95_out_5, n1_bit_multiplier_block_95_out_6, n1_bit_multiplier_block_96_out_5,
       n1_bit_multiplier_block_96_out_6, n1_bit_multiplier_block_97_out_5, n1_bit_multiplier_block_97_out_6,
       n1_bit_multiplier_block_98_out_6, n1_bit_multiplier_block_99_out_6, n1_bit_multiplier_block_100_out_5,
       n1_bit_multiplier_block_100_out_6, n1_bit_multiplier_block_101_out_5,
       n1_bit_multiplier_block_101_out_6, n1_bit_multiplier_block_102_out_5,
       n1_bit_multiplier_block_102_out_6, n1_bit_multiplier_block_103_out_6,
       n1_bit_multiplier_block_104_out_6, n1_bit_multiplier_block_105_out_5,
       n1_bit_multiplier_block_105_out_6, n1_bit_multiplier_block_106_out_5,
       n1_bit_multiplier_block_106_out_6, n1_bit_multiplier_block_109_out_6,
       n1_bit_multiplier_block_110_out_5, n1_bit_multiplier_block_110_out_6,
       n1_bit_multiplier_block_111_out_5, n1_bit_multiplier_block_111_out_6,
       n1_bit_multiplier_block_112_out_6, n1_bit_multiplier_block_113_out_6,
       n1_bit_multiplier_block_114_out_5, n1_bit_multiplier_block_114_out_6,
       n1_bit_multiplier_block_115_out_6, n1_bit_multiplier_block_116_out_6,
       n1_bit_multiplier_block_117_out_5, n1_bit_multiplier_block_117_out_6,
       n1_bit_multiplier_block_118_out_6, n1_bit_multiplier_block_119_out_5,
       n1_bit_multiplier_block_119_out_6, n1_bit_multiplier_block_120_out_5,
       n1_bit_multiplier_block_120_out_6, n1_bit_multiplier_block_121_out_5,
       n1_bit_multiplier_block_122_out_5, n1_bit_multiplier_block_122_out_6,
       n1_bit_multiplier_block_123_out_5, n1_bit_multiplier_block_123_out_6, ppg_1_pp, ppg_2_pp, ppg_3_pp,
       ppg_4_pp, ppg_5_pp, ppg_7_pp, ppg_8_pp, ppg_9_pp, ppg_10_pp, ppg_11_pp, ppg_12_pp, ppg_14_pp,
       ppg_15_pp, ppg_17_pp, ppg_18_pp, ppg_19_pp, ppg_20_pp, ppg_22_pp, ppg_23_pp, ppg_24_pp, ppg_25_pp,
       ppg_27_pp, ppg_28_pp, ppg_29_pp, ppg_30_pp, ppg_32_pp, ppg_33_pp, ppg_34_pp, ppg_36_pp, ppg_37_pp,
       ppg_38_pp, ppg_39_pp, ppg_40_pp, ppg_41_pp, ppg_42_pp, ppg_43_pp, ppg_45_pp, ppg_46_pp, ppg_47_pp,
       ppg_48_pp, ppg_49_pp, ppg_50_pp, ppg_51_pp, ppg_52_pp, ppg_53_pp, ppg_54_pp, ppg_55_pp, ppg_56_pp,
       ppg_57_pp, ppg_58_pp, ppg_59_pp, ppg_60_pp, ppg_61_pp, ppg_62_pp, ppg_63_pp, ppg_64_pp, ppg_65_pp,
       ppg_66_pp, ppg_67_pp, ppg_68_pp, ppg_71_pp, ppg_72_pp, ppg_73_pp, ppg_75_pp, ppg_76_pp, ppg_77_pp,
       ppg_78_pp, ppg_79_pp, ppg_80_pp, ppg_81_pp, ppg_82_pp, ppg_83_pp, ppg_84_pp, ppg_86_pp, ppg_88_pp,
       ppg_89_pp, ppg_90_pp, ppg_91_pp, ppg_92_pp, ppg_93_pp, ppg_94_pp, ppg_95_pp, ppg_96_pp, ppg_97_pp,
       ppg_98_pp, ppg_99_pp, ppg_100_pp, ppg_102_pp, ppg_103_pp, ppg_104_pp, ppg_105_pp, ppg_106_pp,
       ppg_108_pp, ppg_109_pp, ppg_110_pp, ppg_111_pp, ppg_112_pp, ppg_113_pp, ppg_114_pp, ppg_115_pp,
       ppg_116_pp, ppg_117_pp, ppg_118_pp, ppg_119_pp, ppg_120_pp, undriven, undriven_2, undriven_3,
       undriven_4;

  _1_bit_multiplier_block u_1_bit_multiplier_block_1 ();  // open: PP, Sin, en, Cin, out_6, out_5
  control_circuit control_circuit_1 (
    .out_5(control_circuit_1_out_5), .out_6(control_circuit_1_out_6), .out_7(control_circuit_1_out_7),
    .out_8(control_circuit_1_out_8), .out_9(Yi), .out_10(control_circuit_1_out_10),
    .out_11(control_circuit_1_out_11), .out_12(control_circuit_1_out_12), .out_13(control_circuit_1_out_13),
    .out_14(control_circuit_1_out_14), .out_15(control_circuit_1_out_15), .out_16(control_circuit_1_out_16),
    .out_17(control_circuit_1_out_17), .out_18(control_circuit_1_out_18), .out_19(control_circuit_1_out_19),
    .out_20(control_circuit_1_out_20));  // open: ctlA_0, ctlA_1, ctlB_0, ctlB_1
  _1_bit_multiplier_block u_1_bit_multiplier_block_2 (
    .PP(ppg_1_pp), .en(control_circuit_1_out_20), .Cin(n1_bit_multiplier_block_3_out_6),
    .out_5(n1_bit_multiplier_block_2_out_5));  // open: Sin, out_6
  PPG ppg_1 (
    .PP(ppg_1_pp), .Yi(Yi_8), .Yi_1(Yi_1_8), .Y(booth_encoder_8_one), ._2Y(booth_encoder_8_two),
    .NEG(booth_encoder_8_neg));
  _1_bit_multiplier_block u_1_bit_multiplier_block_3 (
    .PP(ppg_2_pp), .en(control_circuit_1_out_20), .Cin(n1_bit_multiplier_block_5_out_6),
    .out_6(n1_bit_multiplier_block_3_out_6), .out_5(n1_bit_multiplier_block_3_out_5));  // open: Sin
  _1_bit_multiplier_block u_1_bit_multiplier_block_4 (
    .PP(ppg_3_pp), .en(control_circuit_1_out_20), .Cin(n1_bit_multiplier_block_6_out_6),
    .out_5(n1_bit_multiplier_block_4_out_5));  // open: Sin, out_6
  PPG ppg_2 (
    .PP(ppg_2_pp), .Yi(Yi_8), .Yi_1(Yi_1_8), .Y(booth_encoder_8_one), ._2Y(booth_encoder_8_two),
    .NEG(booth_encoder_8_neg));
  PPG ppg_3 (
    .PP(ppg_3_pp), .Yi(Yi_7), .Yi_1(Yi_1_7), .Y(booth_encoder_7_one), ._2Y(booth_encoder_7_one),
    .NEG(booth_encoder_7_neg));
  PPG ppg_4 (
    .PP(ppg_4_pp), .Yi(Yi_8), .Yi_1(Yi_1_8), .Y(booth_encoder_8_one), ._2Y(booth_encoder_8_two),
    .NEG(booth_encoder_8_neg));
  _1_bit_multiplier_block u_1_bit_multiplier_block_5 (
    .PP(ppg_4_pp), .Sin(n1_bit_multiplier_block_4_out_5), .en(control_circuit_1_out_20),
    .Cin(n1_bit_multiplier_block_7_out_6), .out_6(n1_bit_multiplier_block_5_out_6),
    .out_5(n1_bit_multiplier_block_5_out_5));
  PPG ppg_5 (
    .PP(ppg_5_pp), .Yi(Yi_7), .Yi_1(Yi_1_7), .Y(booth_encoder_7_one), ._2Y(booth_encoder_7_two),
    .NEG(booth_encoder_7_neg));
  _1_bit_multiplier_block u_1_bit_multiplier_block_6 (
    .PP(ppg_5_pp), .en(control_circuit_1_out_20), .Cin(n1_bit_multiplier_block_9_out_6),
    .out_6(n1_bit_multiplier_block_6_out_6), .out_5(n1_bit_multiplier_block_6_out_5));  // open: Sin
  _1_bit_multiplier_block u_1_bit_multiplier_block_7 (
    .Sin(n1_bit_multiplier_block_6_out_5), .en(control_circuit_1_out_19),
    .Cin(n1_bit_multiplier_block_10_out_6), .out_6(n1_bit_multiplier_block_7_out_6),
    .out_5(n1_bit_multiplier_block_7_out_5));  // open: PP
  _1_bit_multiplier_block u_1_bit_multiplier_block_8 (
    .PP(ppg_7_pp), .Cin(n1_bit_multiplier_block_11_out_6), .out_5(n1_bit_multiplier_block_8_out_5));  // open: Sin, en, out_6
  _1_bit_multiplier_block u_1_bit_multiplier_block_9 (
    .PP(ppg_8_pp), .Sin(n1_bit_multiplier_block_8_out_5), .en(control_circuit_1_out_20),
    .Cin(n1_bit_multiplier_block_12_out_6), .out_6(n1_bit_multiplier_block_9_out_6),
    .out_5(n1_bit_multiplier_block_9_out_5));
  PPG ppg_6 (
    .Yi(Yi_8), .Yi_1(Yi_1_8), .Y(booth_encoder_8_one), ._2Y(booth_encoder_8_two), .NEG(booth_encoder_8_neg));  // open: PP
  _1_bit_multiplier_block u_1_bit_multiplier_block_10 (
    .PP(ppg_9_pp), .Sin(n1_bit_multiplier_block_9_out_5), .en(control_circuit_1_out_19),
    .Cin(n1_bit_multiplier_block_14_out_6), .out_6(n1_bit_multiplier_block_10_out_6),
    .out_5(n1_bit_multiplier_block_10_out_5));
  PPG ppg_7 (
    .PP(ppg_7_pp), .Yi(Yi_6), .Yi_1(Yi_1_6), .Y(booth_encoder_6_one), ._2Y(booth_encoder_6_two),
    .NEG(booth_encoder_6_neg));
  _1_bit_multiplier_block u_1_bit_multiplier_block_11 (
    .PP(ppg_10_pp), .Cin(n1_bit_multiplier_block_15_out_6), .out_6(n1_bit_multiplier_block_11_out_6),
    .out_5(n1_bit_multiplier_block_11_out_5));  // open: Sin, en
  PPG ppg_8 (
    .PP(ppg_8_pp), .Yi(Yi_7), .Yi_1(Yi_1_7), .Y(booth_encoder_7_one), ._2Y(booth_encoder_7_two),
    .NEG(booth_encoder_7_neg));
  _1_bit_multiplier_block u_1_bit_multiplier_block_12 (
    .PP(ppg_11_pp), .Sin(n1_bit_multiplier_block_11_out_5), .en(control_circuit_1_out_19),
    .Cin(n1_bit_multiplier_block_16_out_6), .out_6(n1_bit_multiplier_block_12_out_6),
    .out_5(n1_bit_multiplier_block_12_out_5));
  PPG ppg_9 (
    .PP(ppg_9_pp), .Yi(Yi_8), .Yi_1(Yi_1_8), .Y(booth_encoder_8_one), ._2Y(booth_encoder_8_two),
    .NEG(booth_encoder_8_neg));
  // _1_bit_multiplier_block 1_bit_multiplier_block_13: pin names not known; wires that end beside it: n1_bit_multiplier_block_13_p1, n1_bit_multiplier_block_13_p2, in_28, n1_bit_multiplier_block_13_p4
  PPG ppg_10 (
    .PP(ppg_10_pp), .Yi(Yi_6), .Yi_1(Yi_1_6), .Y(booth_encoder_6_one), ._2Y(booth_encoder_6_two),
    .NEG(booth_encoder_6_neg));
  PPG ppg_11 (
    .PP(ppg_11_pp), .Yi(Yi_7), .Yi_1(Yi_1_7), .Y(booth_encoder_7_one), ._2Y(booth_encoder_7_two),
    .NEG(booth_encoder_7_neg));
  PPG ppg_12 (
    .PP(ppg_12_pp), .Yi(Yi_8), .Yi_1(Yi_1_8), .Y(booth_encoder_8_one), ._2Y(booth_encoder_8_two),
    .NEG(booth_encoder_8_neg));
  _1_bit_multiplier_block u_1_bit_multiplier_block_14 (
    .PP(ppg_12_pp), .Sin(n1_bit_multiplier_block_12_out_5), .en(control_circuit_1_out_19),
    .Cin(n1_bit_multiplier_block_17_out_6), .out_6(n1_bit_multiplier_block_14_out_6),
    .out_5(n1_bit_multiplier_block_14_out_5));
  PPG ppg_13 (
    .Yi(Yi_5), .Yi_1(Yi_1_5), .Y(in_28), ._2Y(n1_bit_multiplier_block_13_p2),
    .NEG(n1_bit_multiplier_block_13_p1));  // open: PP
  PPG ppg_14 (
    .PP(ppg_14_pp), .Yi(Yi_6), .Yi_1(Yi_1_6), .Y(booth_encoder_6_one), ._2Y(booth_encoder_6_two),
    .NEG(booth_encoder_6_neg));
  _1_bit_multiplier_block u_1_bit_multiplier_block_15 (
    .PP(ppg_14_pp), .Cin(n1_bit_multiplier_block_19_out_6), .out_6(n1_bit_multiplier_block_15_out_6),
    .out_5(n1_bit_multiplier_block_15_out_5));  // open: Sin, en
  PPG ppg_15 (
    .PP(ppg_15_pp), .Yi(Yi_7), .Yi_1(Yi_1_7), .Y(booth_encoder_7_one), ._2Y(booth_encoder_7_two),
    .NEG(booth_encoder_7_neg));
  _1_bit_multiplier_block u_1_bit_multiplier_block_16 (
    .PP(ppg_15_pp), .Sin(n1_bit_multiplier_block_15_out_5), .en(control_circuit_1_out_19),
    .Cin(n1_bit_multiplier_block_20_out_6), .out_6(n1_bit_multiplier_block_16_out_6),
    .out_5(n1_bit_multiplier_block_16_out_5));
  _1_bit_multiplier_block u_1_bit_multiplier_block_17 (
    .PP(ppg_17_pp), .Sin(n1_bit_multiplier_block_16_out_5), .en(control_circuit_1_out_19),
    .Cin(n1_bit_multiplier_block_21_out_6), .out_6(n1_bit_multiplier_block_17_out_6),
    .out_5(n1_bit_multiplier_block_17_out_5));
  PPG ppg_16 (
    .Yi(Yi_5), .Yi_1(Yi_1_5), .Y(in_28), ._2Y(n1_bit_multiplier_block_13_p2),
    .NEG(n1_bit_multiplier_block_13_p1));  // open: PP
  _1_bit_multiplier_block u_1_bit_multiplier_block_18 (
    .Cin(n1_bit_multiplier_block_23_out_6), .out_6(n1_bit_multiplier_block_13_p4));  // open: PP, Sin, en, out_5
  _1_bit_multiplier_block u_1_bit_multiplier_block_19 (
    .PP(ppg_18_pp), .Cin(n1_bit_multiplier_block_24_out_6), .out_6(n1_bit_multiplier_block_19_out_6),
    .out_5(n1_bit_multiplier_block_19_out_5));  // open: Sin, en
  _1_bit_multiplier_block u_1_bit_multiplier_block_20 (
    .PP(ppg_19_pp), .Sin(n1_bit_multiplier_block_19_out_5), .en(control_circuit_1_out_19),
    .Cin(n1_bit_multiplier_block_25_out_6), .out_6(n1_bit_multiplier_block_20_out_6),
    .out_5(n1_bit_multiplier_block_20_out_5));
  PPG ppg_17 (
    .PP(ppg_17_pp), .Yi(Yi_8), .Yi_1(Yi_1_8), .Y(booth_encoder_8_one), ._2Y(booth_encoder_8_two),
    .NEG(booth_encoder_8_neg));
  _1_bit_multiplier_block u_1_bit_multiplier_block_21 (
    .PP(ppg_20_pp), .Sin(n1_bit_multiplier_block_20_out_5), .en(control_circuit_1_out_18),
    .Cin(n1_bit_multiplier_block_26_out_6), .out_6(n1_bit_multiplier_block_21_out_6),
    .out_5(n1_bit_multiplier_block_21_out_5));
  // _1_bit_multiplier_block 1_bit_multiplier_block_22: pin names not known; wires that end beside it: n1_bit_multiplier_block_22_p1, n1_bit_multiplier_block_22_p2, n1_bit_multiplier_block_22_p3, n1_bit_multiplier_block_22_p4, n1_bit_multiplier_block_22_p5
  _1_bit_multiplier_block u_1_bit_multiplier_block_23 (
    .PP(ppg_22_pp), .Sin(n1_bit_multiplier_block_22_p4), .Cin(n1_bit_multiplier_block_28_out_6),
    .out_6(n1_bit_multiplier_block_23_out_6));  // open: en, out_5
  PPG ppg_18 (
    .PP(ppg_18_pp), .Yi(Yi_6), .Yi_1(Yi_1_6), .Y(booth_encoder_6_one), ._2Y(booth_encoder_6_two),
    .NEG(booth_encoder_6_neg));
  _1_bit_multiplier_block u_1_bit_multiplier_block_24 (
    .PP(ppg_23_pp), .Cin(n1_bit_multiplier_block_30_out_6), .out_6(n1_bit_multiplier_block_24_out_6),
    .out_5(n1_bit_multiplier_block_24_out_5));  // open: Sin, en
  PPG ppg_19 (
    .PP(ppg_19_pp), .Yi(Yi_7), .Yi_1(Yi_1_7), .Y(booth_encoder_7_one), ._2Y(booth_encoder_7_two),
    .NEG(booth_encoder_7_neg));
  _1_bit_multiplier_block u_1_bit_multiplier_block_25 (
    .PP(ppg_24_pp), .Sin(n1_bit_multiplier_block_24_out_5), .en(control_circuit_1_out_19),
    .Cin(n1_bit_multiplier_block_31_out_6), .out_6(n1_bit_multiplier_block_25_out_6),
    .out_5(n1_bit_multiplier_block_25_out_5));
  PPG ppg_20 (
    .PP(ppg_20_pp), .Yi(Yi_8), .Yi_1(Yi_1_8), .Y(booth_encoder_8_one), ._2Y(booth_encoder_8_two),
    .NEG(booth_encoder_8_neg));
  _1_bit_multiplier_block u_1_bit_multiplier_block_26 (
    .PP(ppg_25_pp), .Sin(n1_bit_multiplier_block_25_out_5), .en(control_circuit_1_out_18),
    .Cin(control_circuit_1_out_18), .out_6(n1_bit_multiplier_block_26_out_6),
    .out_5(n1_bit_multiplier_block_26_out_5));
  PPG ppg_21 (
    .Yi(Yi_4), .Yi_1(Yi_1_4), .Y(n1_bit_multiplier_block_27_p1), ._2Y(n1_bit_multiplier_block_22_p2),
    .NEG(n1_bit_multiplier_block_22_p1));  // open: PP
  // _1_bit_multiplier_block 1_bit_multiplier_block_27: pin names not known; wires that end beside it: n1_bit_multiplier_block_27_p1, n1_bit_multiplier_block_22_p5, n1_bit_multiplier_block_27_p3, n1_bit_multiplier_block_27_p4
  PPG ppg_22 (
    .PP(ppg_22_pp), .Yi(Yi_5), .Yi_1(Yi_1_5), .Y(in_28), ._2Y(n1_bit_multiplier_block_13_p2),
    .NEG(n1_bit_multiplier_block_13_p1));
  _1_bit_multiplier_block u_1_bit_multiplier_block_28 (
    .PP(ppg_27_pp), .Sin(n1_bit_multiplier_block_27_p3), .Cin(n1_bit_multiplier_block_34_out_6),
    .out_6(n1_bit_multiplier_block_28_out_6));  // open: en, out_5
  PPG ppg_23 (
    .PP(ppg_23_pp), .Yi(Yi_6), .Yi_1(Yi_1_6), .Y(booth_encoder_6_one), ._2Y(booth_encoder_6_two),
    .NEG(booth_encoder_6_neg));
  PPG ppg_24 (
    .PP(ppg_24_pp), .Yi(Yi_7), .Yi_1(Yi_1_7), .Y(booth_encoder_7_one), ._2Y(booth_encoder_7_two),
    .NEG(booth_encoder_7_neg));
  PPG ppg_25 (
    .PP(ppg_25_pp), .Yi(Yi_8), .Yi_1(Yi_1_8), .Y(booth_encoder_8_one), ._2Y(booth_encoder_8_two),
    .NEG(booth_encoder_8_neg));
  // _1_bit_multiplier_block 1_bit_multiplier_block_29: pin names not known; wires that end beside it: n1_bit_multiplier_block_29_p1, n1_bit_multiplier_block_29_p2, n1_bit_multiplier_block_29_p3, n1_bit_multiplier_block_29_p4, n1_bit_multiplier_block_29_p5
  PPG ppg_26 (
    .Yi(Yi_4), .Yi_1(Yi_1_4), .Y(n1_bit_multiplier_block_22_p3), ._2Y(n1_bit_multiplier_block_22_p2),
    .NEG(n1_bit_multiplier_block_22_p1));  // open: PP
  PPG ppg_27 (
    .PP(ppg_27_pp), .Yi(Yi_5), .Yi_1(Yi_1_5), .Y(in_28), ._2Y(n1_bit_multiplier_block_13_p2),
    .NEG(n1_bit_multiplier_block_13_p1));
  PPG ppg_28 (
    .PP(ppg_28_pp), .Yi(Yi_6), .Yi_1(Yi_1_6), .Y(booth_encoder_6_one), ._2Y(booth_encoder_6_two),
    .NEG(booth_encoder_6_neg));
  _1_bit_multiplier_block u_1_bit_multiplier_block_30 (
    .PP(ppg_28_pp), .Cin(n1_bit_multiplier_block_35_out_6), .out_6(n1_bit_multiplier_block_30_out_6));  // open: Sin, en, out_5
  PPG ppg_29 (
    .PP(ppg_29_pp), .Yi(Yi_7), .Yi_1(Yi_1_7), .Y(booth_encoder_7_one), ._2Y(booth_encoder_7_two),
    .NEG(booth_encoder_7_neg));
  _1_bit_multiplier_block u_1_bit_multiplier_block_31 (
    .PP(ppg_29_pp), .en(control_circuit_1_out_18), .Cin(n1_bit_multiplier_block_36_out_6),
    .out_6(n1_bit_multiplier_block_31_out_6), .out_5(n1_bit_multiplier_block_31_out_5));  // open: Sin
  PPG ppg_30 (
    .PP(ppg_30_pp), .Yi(Yi_8), .Yi_1(Yi_1_8), .Y(booth_encoder_8_one), ._2Y(booth_encoder_8_two),
    .NEG(booth_encoder_8_neg));
  _1_bit_multiplier_block u_1_bit_multiplier_block_32 (
    .PP(ppg_30_pp), .Sin(n1_bit_multiplier_block_31_out_5), .en(control_circuit_1_out_18),
    .Cin(n1_bit_multiplier_block_37_out_6), .out_6(control_circuit_1_out_18),
    .out_5(n1_bit_multiplier_block_32_out_5));
  PPG ppg_31 (
    .Yi(Yi_3), .Yi_1(Yi_1_3), .Y(n1_bit_multiplier_block_29_p5), ._2Y(n1_bit_multiplier_block_29_p4),
    .NEG(n1_bit_multiplier_block_29_p3));  // open: PP
  PPG ppg_32 (
    .PP(ppg_32_pp), .Yi(Yi_4), .Yi_1(Yi_1_4), .Y(n1_bit_multiplier_block_22_p3),
    ._2Y(n1_bit_multiplier_block_22_p2), .NEG(n1_bit_multiplier_block_22_p1));
  _1_bit_multiplier_block u_1_bit_multiplier_block_33 (
    .PP(ppg_32_pp), .Sin(n1_bit_multiplier_block_29_p1), .Cin(n1_bit_multiplier_block_39_out_6),
    .out_6(n1_bit_multiplier_block_27_p4), .out_5(n1_bit_multiplier_block_33_out_5));  // open: en
  PPG ppg_33 (
    .PP(ppg_33_pp), .Yi(Yi_5), .Yi_1(Yi_1_5), .Y(in_28), ._2Y(n1_bit_multiplier_block_13_p2),
    .NEG(n1_bit_multiplier_block_13_p1));
  _1_bit_multiplier_block u_1_bit_multiplier_block_34 (
    .PP(ppg_33_pp), .Sin(n1_bit_multiplier_block_33_out_5), .Cin(n1_bit_multiplier_block_40_out_6),
    .out_6(n1_bit_multiplier_block_34_out_6));  // open: en, out_5
  _1_bit_multiplier_block u_1_bit_multiplier_block_35 (
    .PP(ppg_36_pp), .Cin(n1_bit_multiplier_block_41_out_6), .out_6(n1_bit_multiplier_block_35_out_6),
    .out_5(n1_bit_multiplier_block_35_out_5));  // open: Sin, en
  _1_bit_multiplier_block u_1_bit_multiplier_block_36 (
    .PP(ppg_37_pp), .Sin(n1_bit_multiplier_block_35_out_5), .en(control_circuit_1_out_18),
    .Cin(n1_bit_multiplier_block_42_out_6), .out_6(n1_bit_multiplier_block_36_out_6),
    .out_5(n1_bit_multiplier_block_36_out_5));
  PPG ppg_34 (
    .PP(ppg_34_pp), .Yi(Yi_8), .Yi_1(Yi_1_8), .Y(booth_encoder_8_one), ._2Y(booth_encoder_8_two),
    .NEG(booth_encoder_8_neg));
  _1_bit_multiplier_block u_1_bit_multiplier_block_37 (
    .PP(ppg_34_pp), .Sin(n1_bit_multiplier_block_36_out_5), .en(control_circuit_1_out_18),
    .Cin(n1_bit_multiplier_block_43_out_6), .out_6(n1_bit_multiplier_block_37_out_6),
    .out_5(n1_bit_multiplier_block_37_out_5));
  PPG ppg_35 (
    .Yi(Yi_3), .Yi_1(Yi_1_3), .Y(n1_bit_multiplier_block_29_p5), ._2Y(n1_bit_multiplier_block_29_p4),
    .NEG(n1_bit_multiplier_block_29_p3));  // open: PP
  _1_bit_multiplier_block u_1_bit_multiplier_block_38 (
    .Cin(n1_bit_multiplier_block_45_out_6), .out_6(n1_bit_multiplier_block_29_p2),
    .out_5(n1_bit_multiplier_block_38_out_5));  // open: PP, Sin, en
  _1_bit_multiplier_block u_1_bit_multiplier_block_39 (
    .PP(ppg_38_pp), .Sin(n1_bit_multiplier_block_38_out_5), .Cin(n1_bit_multiplier_block_46_out_6),
    .out_6(n1_bit_multiplier_block_39_out_6), .out_5(n1_bit_multiplier_block_39_out_5));  // open: en
  _1_bit_multiplier_block u_1_bit_multiplier_block_40 (
    .PP(ppg_39_pp), .Sin(n1_bit_multiplier_block_39_out_5), .Cin(n1_bit_multiplier_block_47_out_6),
    .out_6(n1_bit_multiplier_block_40_out_6));  // open: en, out_5
  PPG ppg_36 (
    .PP(ppg_36_pp), .Yi(Yi_6), .Yi_1(Yi_1_6), .Y(booth_encoder_6_one), ._2Y(booth_encoder_6_two),
    .NEG(booth_encoder_6_neg));
  _1_bit_multiplier_block u_1_bit_multiplier_block_41 (
    .PP(ppg_40_pp), .Cin(n1_bit_multiplier_block_48_out_6), .out_6(n1_bit_multiplier_block_41_out_6),
    .out_5(n1_bit_multiplier_block_41_out_5));  // open: Sin, en
  PPG ppg_37 (
    .PP(ppg_37_pp), .Yi(Yi_7), .Yi_1(Yi_1_7), .Y(booth_encoder_7_one), ._2Y(booth_encoder_7_two),
    .NEG(booth_encoder_7_neg));
  _1_bit_multiplier_block u_1_bit_multiplier_block_42 (
    .PP(ppg_41_pp), .Sin(n1_bit_multiplier_block_41_out_5), .en(control_circuit_1_out_18),
    .Cin(n1_bit_multiplier_block_49_out_6), .out_6(n1_bit_multiplier_block_42_out_6),
    .out_5(control_circuit_1_out_17));
  _1_bit_multiplier_block u_1_bit_multiplier_block_43 (
    .PP(ppg_42_pp), .Sin(control_circuit_1_out_17), .en(control_circuit_1_out_17),
    .Cin(n1_bit_multiplier_block_50_out_6), .out_6(n1_bit_multiplier_block_43_out_6),
    .out_5(n1_bit_multiplier_block_43_out_5));
  _1_bit_multiplier_block u_1_bit_multiplier_block_44 (
    .PP(ppg_43_pp), .en(control_circuit_1_out_8), .Cin(n1_bit_multiplier_block_51_out_6));  // open: Sin, out_6, out_5
  _1_bit_multiplier_block u_1_bit_multiplier_block_45 (
    .Cin(n1_bit_multiplier_block_52_out_6), .out_6(n1_bit_multiplier_block_45_out_6),
    .out_5(n1_bit_multiplier_block_45_out_5));  // open: PP, Sin, en
  PPG ppg_38 (
    .PP(ppg_38_pp), .Yi(Yi_4), .Yi_1(Yi_1_4), .Y(n1_bit_multiplier_block_22_p3),
    ._2Y(n1_bit_multiplier_block_22_p2), .NEG(n1_bit_multiplier_block_22_p1));
  _1_bit_multiplier_block u_1_bit_multiplier_block_46 (
    .PP(ppg_45_pp), .Sin(n1_bit_multiplier_block_45_out_5), .Cin(n1_bit_multiplier_block_54_out_6),
    .out_6(n1_bit_multiplier_block_46_out_6), .out_5(n1_bit_multiplier_block_46_out_5));  // open: en
  PPG ppg_39 (
    .PP(ppg_39_pp), .Yi(Yi_5), .Yi_1(Yi_1_5), .Y(in_28), ._2Y(n1_bit_multiplier_block_13_p2),
    .NEG(n1_bit_multiplier_block_13_p1));
  _1_bit_multiplier_block u_1_bit_multiplier_block_47 (
    .PP(ppg_46_pp), .Sin(n1_bit_multiplier_block_46_out_5), .Cin(n1_bit_multiplier_block_55_out_6),
    .out_6(n1_bit_multiplier_block_47_out_6));  // open: en, out_5
  PPG ppg_40 (
    .PP(ppg_40_pp), .Yi(Yi_6), .Yi_1(Yi_1_6), .Y(booth_encoder_6_one), ._2Y(booth_encoder_6_two),
    .NEG(booth_encoder_6_neg));
  _1_bit_multiplier_block u_1_bit_multiplier_block_48 (
    .PP(ppg_47_pp), .Cin(n1_bit_multiplier_block_56_out_6), .out_6(n1_bit_multiplier_block_48_out_6),
    .out_5(n1_bit_multiplier_block_48_out_5));  // open: Sin, en
  PPG ppg_41 (
    .PP(ppg_41_pp), .Yi(Yi_7), .Yi_1(Yi_1_7), .Y(booth_encoder_7_one), ._2Y(booth_encoder_7_two),
    .NEG(booth_encoder_7_neg));
  _1_bit_multiplier_block u_1_bit_multiplier_block_49 (
    .PP(ppg_48_pp), .Sin(n1_bit_multiplier_block_48_out_5), .en(control_circuit_1_out_18),
    .Cin(n1_bit_multiplier_block_57_out_6), .out_6(n1_bit_multiplier_block_49_out_6),
    .out_5(n1_bit_multiplier_block_49_out_5));
  PPG ppg_42 (
    .PP(ppg_42_pp), .Yi(Yi_8), .Yi_1(Yi_1_8), .Y(booth_encoder_8_one), ._2Y(booth_encoder_8_two),
    .NEG(booth_encoder_8_neg));
  _1_bit_multiplier_block u_1_bit_multiplier_block_50 (
    .PP(ppg_49_pp), .Sin(n1_bit_multiplier_block_49_out_5), .en(control_circuit_1_out_17),
    .Cin(n1_bit_multiplier_block_58_out_6), .out_6(n1_bit_multiplier_block_50_out_6),
    .out_5(n1_bit_multiplier_block_50_out_5));
  PPG ppg_43 (
    .PP(ppg_43_pp), .Yi(Yi_2), .Yi_1(Yi_1_2), .Y(booth_encoder_2_one), ._2Y(booth_encoder_2_two),
    .NEG(booth_encoder_2_neg));
  _1_bit_multiplier_block u_1_bit_multiplier_block_51 (
    .PP(ppg_50_pp), .en(control_circuit_1_out_8), .Cin(control_circuit_1_out_8),
    .out_6(n1_bit_multiplier_block_51_out_6));  // open: Sin, out_5
  PPG ppg_44 (
    .Yi(Yi_3), .Yi_1(Yi_1_3), .Y(n1_bit_multiplier_block_29_p5), ._2Y(n1_bit_multiplier_block_29_p4),
    .NEG(n1_bit_multiplier_block_29_p3));  // open: PP
  _1_bit_multiplier_block u_1_bit_multiplier_block_52 (
    .PP(ppg_51_pp), .Cin(n1_bit_multiplier_block_60_out_6), .out_6(n1_bit_multiplier_block_52_out_6),
    .out_5(n1_bit_multiplier_block_52_out_5));  // open: Sin, en
  PPG ppg_45 (
    .PP(ppg_45_pp), .Yi(Yi_4), .Yi_1(Yi_1_4), .Y(n1_bit_multiplier_block_22_p3),
    ._2Y(n1_bit_multiplier_block_22_p1), .NEG(n1_bit_multiplier_block_22_p1));
  PPG ppg_46 (
    .PP(ppg_46_pp), .Yi(Yi_5), .Yi_1(Yi_1_5), .Y(in_28), ._2Y(n1_bit_multiplier_block_13_p2),
    .NEG(n1_bit_multiplier_block_13_p1));
  PPG ppg_47 (
    .PP(ppg_47_pp), .Yi(Yi_6), .Yi_1(Yi_1_6), .Y(booth_encoder_6_one), ._2Y(booth_encoder_6_two),
    .NEG(booth_encoder_6_neg));
  PPG ppg_48 (
    .PP(ppg_48_pp), .Yi(Yi_7), .Yi_1(Yi_1_7), .Y(booth_encoder_7_one), ._2Y(booth_encoder_7_two),
    .NEG(booth_encoder_7_neg));
  PPG ppg_49 (
    .PP(ppg_49_pp), .Yi(Yi_8), .Yi_1(Yi_1_8), .Y(booth_encoder_8_one), ._2Y(booth_encoder_8_two),
    .NEG(booth_encoder_8_neg));
  _1_bit_multiplier_block u_1_bit_multiplier_block_53 (
    .PP(ppg_57_pp), .en(control_circuit_1_out_8), .Cin(n1_bit_multiplier_block_66_out_6));  // open: Sin, out_6, out_5
  PPG ppg_50 (
    .PP(ppg_50_pp), .Yi(Yi_2), .Yi_1(Yi_1_2), .Y(booth_encoder_2_one), ._2Y(booth_encoder_2_two),
    .NEG(booth_encoder_2_neg));
  PPG ppg_51 (
    .PP(ppg_51_pp), .Yi(Yi_3), .Yi_1(Yi_1_3), .Y(n1_bit_multiplier_block_29_p5),
    ._2Y(n1_bit_multiplier_block_29_p4), .NEG(n1_bit_multiplier_block_29_p3));
  PPG ppg_52 (
    .PP(ppg_52_pp), .Yi(Yi_4), .Yi_1(Yi_1_4), .Y(n1_bit_multiplier_block_22_p3),
    ._2Y(n1_bit_multiplier_block_22_p2), .NEG(n1_bit_multiplier_block_22_p1));
  _1_bit_multiplier_block u_1_bit_multiplier_block_54 (
    .PP(ppg_52_pp), .Sin(n1_bit_multiplier_block_52_out_5), .Cin(n1_bit_multiplier_block_61_out_6),
    .out_6(n1_bit_multiplier_block_54_out_6), .out_5(n1_bit_multiplier_block_54_out_5));  // open: en
  PPG ppg_53 (
    .PP(ppg_53_pp), .Yi(Yi_5), .Yi_1(Yi_1_5), .Y(in_28), ._2Y(n1_bit_multiplier_block_13_p2),
    .NEG(n1_bit_multiplier_block_13_p1));
  _1_bit_multiplier_block u_1_bit_multiplier_block_55 (
    .PP(ppg_53_pp), .Sin(n1_bit_multiplier_block_54_out_5), .Cin(n1_bit_multiplier_block_62_out_6),
    .out_6(n1_bit_multiplier_block_55_out_6));  // open: en, out_5
  PPG ppg_54 (
    .PP(ppg_54_pp), .Yi(Yi_6), .Yi_1(Yi_1_6), .Y(booth_encoder_6_one), ._2Y(booth_encoder_6_two),
    .NEG(booth_encoder_6_neg));
  _1_bit_multiplier_block u_1_bit_multiplier_block_56 (
    .PP(ppg_54_pp), .Cin(n1_bit_multiplier_block_63_out_6), .out_6(n1_bit_multiplier_block_56_out_6),
    .out_5(n1_bit_multiplier_block_56_out_5));  // open: Sin, en
  PPG ppg_55 (
    .PP(ppg_55_pp), .Yi(Yi_7), .Yi_1(Yi_1_7), .Y(booth_encoder_7_one), ._2Y(booth_encoder_7_two),
    .NEG(booth_encoder_7_neg));
  _1_bit_multiplier_block u_1_bit_multiplier_block_57 (
    .PP(ppg_55_pp), .Sin(n1_bit_multiplier_block_56_out_5), .en(control_circuit_1_out_17),
    .Cin(n1_bit_multiplier_block_64_out_6), .out_6(n1_bit_multiplier_block_57_out_6),
    .out_5(n1_bit_multiplier_block_57_out_5));
  PPG ppg_56 (
    .PP(ppg_56_pp), .Yi(Yi_8), .Yi_1(Yi_1_8), .Y(booth_encoder_8_one), ._2Y(booth_encoder_8_two),
    .NEG(booth_encoder_8_neg));
  _1_bit_multiplier_block u_1_bit_multiplier_block_58 (
    .PP(ppg_56_pp), .Sin(n1_bit_multiplier_block_57_out_5), .en(control_circuit_1_out_17),
    .Cin(n1_bit_multiplier_block_65_out_6), .out_6(n1_bit_multiplier_block_58_out_6),
    .out_5(n1_bit_multiplier_block_58_out_5));
  PPG ppg_57 (.PP(ppg_57_pp), .Yi(Yi), .Yi_1(Yi), .Y(Yi), ._2Y(Yi), .NEG(Yi));
  PPG ppg_58 (
    .PP(ppg_58_pp), .Yi(Yi_2), .Yi_1(Yi_1_2), .Y(booth_encoder_2_one), ._2Y(booth_encoder_2_two),
    .NEG(booth_encoder_2_neg));
  _1_bit_multiplier_block u_1_bit_multiplier_block_59 (
    .PP(ppg_58_pp), .en(control_circuit_1_out_8), .Cin(n1_bit_multiplier_block_67_out_6));  // open: Sin, out_6, out_5
  PPG ppg_59 (
    .PP(ppg_59_pp), .Yi(Yi_3), .Yi_1(Yi_1_3), .Y(n1_bit_multiplier_block_29_p5),
    ._2Y(n1_bit_multiplier_block_29_p4), .NEG(n1_bit_multiplier_block_29_p3));
  _1_bit_multiplier_block u_1_bit_multiplier_block_60 (
    .PP(ppg_59_pp), .Cin(n1_bit_multiplier_block_68_out_6), .out_6(n1_bit_multiplier_block_60_out_6),
    .out_5(n1_bit_multiplier_block_60_out_5));  // open: Sin, en
  _1_bit_multiplier_block u_1_bit_multiplier_block_61 (
    .PP(ppg_62_pp), .Sin(n1_bit_multiplier_block_60_out_5), .Cin(n1_bit_multiplier_block_69_out_6),
    .out_6(n1_bit_multiplier_block_61_out_6), .out_5(n1_bit_multiplier_block_61_out_5));  // open: en
  _1_bit_multiplier_block u_1_bit_multiplier_block_62 (
    .PP(ppg_63_pp), .Sin(n1_bit_multiplier_block_61_out_5), .Cin(n1_bit_multiplier_block_70_out_6),
    .out_6(n1_bit_multiplier_block_62_out_6));  // open: en, out_5
  PPG ppg_60 (
    .PP(ppg_60_pp), .Yi(Yi_6), .Yi_1(Yi_1_6), .Y(n1_bit_multiplier_block_71_p1), ._2Y(booth_encoder_6_two),
    .NEG(booth_encoder_6_neg));
  _1_bit_multiplier_block u_1_bit_multiplier_block_63 (
    .PP(ppg_60_pp), .Cin(n1_bit_multiplier_block_71_p2), .out_6(n1_bit_multiplier_block_63_out_6),
    .out_5(n1_bit_multiplier_block_63_out_5));  // open: Sin, en
  _1_bit_multiplier_block u_1_bit_multiplier_block_64 (
    .PP(ppg_64_pp), .Sin(n1_bit_multiplier_block_63_out_5), .en(control_circuit_1_out_17),
    .Cin(n1_bit_multiplier_block_72_out_6), .out_6(n1_bit_multiplier_block_64_out_6),
    .out_5(n1_bit_multiplier_block_64_out_5));
  _1_bit_multiplier_block u_1_bit_multiplier_block_65 (
    .PP(ppg_65_pp), .Sin(n1_bit_multiplier_block_64_out_5), .en(control_circuit_1_out_17),
    .out_6(n1_bit_multiplier_block_65_out_6), .out_5(n1_bit_multiplier_block_65_out_5));  // open: Cin
  PPG ppg_61 (.PP(ppg_61_pp), .Yi(Yi), .Yi_1(Yi), .Y(Yi), ._2Y(Yi), .NEG(Yi));
  _1_bit_multiplier_block u_1_bit_multiplier_block_66 (
    .PP(ppg_61_pp), .en(control_circuit_1_out_8), .Cin(n1_bit_multiplier_block_73_out_6),
    .out_6(n1_bit_multiplier_block_66_out_6));  // open: Sin, out_5
  _1_bit_multiplier_block u_1_bit_multiplier_block_67 (
    .PP(ppg_66_pp), .en(control_circuit_1_out_7), .Cin(n1_bit_multiplier_block_74_out_6),
    .out_6(n1_bit_multiplier_block_67_out_6));  // open: Sin, out_5
  _1_bit_multiplier_block u_1_bit_multiplier_block_68 (
    .PP(ppg_67_pp), .Cin(n1_bit_multiplier_block_75_out_6), .out_6(n1_bit_multiplier_block_68_out_6),
    .out_5(n1_bit_multiplier_block_68_out_5));  // open: Sin, en
  PPG ppg_62 (
    .PP(ppg_62_pp), .Yi(Yi_4), .Yi_1(Yi_1_4), .Y(n1_bit_multiplier_block_22_p3),
    ._2Y(n1_bit_multiplier_block_22_p2), .NEG(n1_bit_multiplier_block_22_p1));
  _1_bit_multiplier_block u_1_bit_multiplier_block_69 (
    .PP(ppg_68_pp), .Sin(n1_bit_multiplier_block_68_out_5), .Cin(n1_bit_multiplier_block_76_out_6),
    .out_6(n1_bit_multiplier_block_69_out_6));  // open: en, out_5
  PPG ppg_63 (
    .PP(ppg_63_pp), .Yi(Yi_5), .Yi_1(Yi_1_5), .Y(in_28), ._2Y(n1_bit_multiplier_block_13_p2),
    .NEG(n1_bit_multiplier_block_13_p1));
  _1_bit_multiplier_block u_1_bit_multiplier_block_70 (
    .Cin(n1_bit_multiplier_block_77_out_6), .out_6(n1_bit_multiplier_block_70_out_6));  // open: PP, Sin, en, out_5
  // _1_bit_multiplier_block 1_bit_multiplier_block_71: pin names not known; wires that end beside it: n1_bit_multiplier_block_71_p1, n1_bit_multiplier_block_71_p2, n1_bit_multiplier_block_71_p3, n1_bit_multiplier_block_71_p4, n1_bit_multiplier_block_71_p5
  PPG ppg_64 (
    .PP(ppg_64_pp), .Yi(Yi_7), .Yi_1(Yi_1_7), .Y(booth_encoder_7_one), ._2Y(booth_encoder_7_two),
    .NEG(booth_encoder_7_neg));
  _1_bit_multiplier_block u_1_bit_multiplier_block_72 (
    .PP(ppg_71_pp), .Sin(n1_bit_multiplier_block_71_p3), .en(control_circuit_1_out_17),
    .Cin(n1_bit_multiplier_block_79_out_6), .out_6(n1_bit_multiplier_block_72_out_6),
    .out_5(n1_bit_multiplier_block_72_out_5));
  PPG ppg_65 (
    .PP(ppg_65_pp), .Yi(Yi_8), .Yi_1(Yi_1_8), .Y(booth_encoder_8_one), ._2Y(booth_encoder_8_two),
    .NEG(booth_encoder_8_neg));
  _1_bit_multiplier_block u_1_bit_multiplier_block_73 (
    .PP(ppg_72_pp), .en(control_circuit_1_out_8), .Cin(n1_bit_multiplier_block_80_out_6),
    .out_6(n1_bit_multiplier_block_73_out_6));  // open: Sin, out_5
  PPG ppg_66 (
    .PP(ppg_66_pp), .Yi(Yi_2), .Yi_1(Yi_1_2), .Y(booth_encoder_2_one), ._2Y(booth_encoder_2_two),
    .NEG(booth_encoder_2_neg));
  _1_bit_multiplier_block u_1_bit_multiplier_block_74 (
    .PP(ppg_73_pp), .en(control_circuit_1_out_7), .Cin(n1_bit_multiplier_block_82_out_6),
    .out_6(n1_bit_multiplier_block_74_out_6));  // open: Sin, out_5
  PPG ppg_67 (
    .PP(ppg_67_pp), .Yi(Yi_3), .Yi_1(Yi_1_3), .Y(n1_bit_multiplier_block_29_p5),
    ._2Y(n1_bit_multiplier_block_29_p4), .NEG(n1_bit_multiplier_block_29_p3));
  _1_bit_multiplier_block u_1_bit_multiplier_block_75 (
    .Cin(n1_bit_multiplier_block_83_out_6), .out_6(n1_bit_multiplier_block_75_out_6),
    .out_5(n1_bit_multiplier_block_75_out_5));  // open: PP, Sin, en
  PPG ppg_68 (
    .PP(ppg_68_pp), .Yi(Yi_4), .Yi_1(Yi_1_4), .Y(n1_bit_multiplier_block_22_p3),
    ._2Y(n1_bit_multiplier_block_22_p2), .NEG(n1_bit_multiplier_block_22_p1));
  _1_bit_multiplier_block u_1_bit_multiplier_block_76 (
    .PP(ppg_75_pp), .Sin(n1_bit_multiplier_block_75_out_5), .Cin(n1_bit_multiplier_block_84_out_6),
    .out_6(n1_bit_multiplier_block_76_out_6), .out_5(n1_bit_multiplier_block_76_out_5));  // open: en
  PPG ppg_69 (
    .Yi(Yi_5), .Yi_1(Yi_1_5), .Y(in_28), ._2Y(n1_bit_multiplier_block_13_p2),
    .NEG(n1_bit_multiplier_block_13_p1));  // open: PP
  _1_bit_multiplier_block u_1_bit_multiplier_block_77 (
    .PP(ppg_76_pp), .Sin(n1_bit_multiplier_block_76_out_5), .Cin(n1_bit_multiplier_block_85_out_6),
    .out_6(n1_bit_multiplier_block_77_out_6));  // open: en, out_5
  PPG ppg_70 (
    .PP(n1_bit_multiplier_block_71_p4), .Yi(Yi_6), .Yi_1(Yi_1_6), .Y(booth_encoder_6_one),
    ._2Y(booth_encoder_6_two), .NEG(booth_encoder_6_neg));
  _1_bit_multiplier_block u_1_bit_multiplier_block_78 (
    .PP(ppg_77_pp), .Cin(n1_bit_multiplier_block_86_out_6), .out_6(n1_bit_multiplier_block_71_p5),
    .out_5(n1_bit_multiplier_block_78_out_5));  // open: Sin, en
  PPG ppg_71 (
    .PP(ppg_71_pp), .Yi(Yi_7), .Yi_1(Yi_1_7), .Y(booth_encoder_7_one), ._2Y(booth_encoder_7_two),
    .NEG(booth_encoder_7_neg));
  _1_bit_multiplier_block u_1_bit_multiplier_block_79 (
    .PP(ppg_78_pp), .Sin(n1_bit_multiplier_block_78_out_5), .en(control_circuit_1_out_17),
    .out_6(n1_bit_multiplier_block_79_out_6), .out_5(n1_bit_multiplier_block_79_out_5));  // open: Cin
  PPG ppg_72 (.PP(ppg_72_pp), .Yi(Yi), .Yi_1(Yi), .Y(Yi), ._2Y(Yi), .NEG(Yi));
  _1_bit_multiplier_block u_1_bit_multiplier_block_80 (
    .PP(ppg_79_pp), .en(control_circuit_1_out_7), .Cin(n1_bit_multiplier_block_87_out_6),
    .out_6(n1_bit_multiplier_block_80_out_6));  // open: Sin, out_5
  PPG ppg_73 (
    .PP(ppg_73_pp), .Yi(Yi_2), .Yi_1(Yi_1_2), .Y(booth_encoder_2_one), ._2Y(booth_encoder_2_two),
    .NEG(booth_encoder_2_neg));
  PPG ppg_74 (
    .Yi(Yi_3), .Yi_1(Yi_1_3), .Y(n1_bit_multiplier_block_29_p5), ._2Y(n1_bit_multiplier_block_29_p4),
    .NEG(n1_bit_multiplier_block_29_p3));  // open: PP
  PPG ppg_75 (
    .PP(ppg_75_pp), .Yi(Yi_4), .Yi_1(Yi_1_4), .Y(n1_bit_multiplier_block_22_p3),
    ._2Y(n1_bit_multiplier_block_22_p2), .NEG(n1_bit_multiplier_block_22_p1));
  PPG ppg_76 (
    .PP(ppg_76_pp), .Yi(Yi_5), .Yi_1(Yi_1_5), .Y(in_28), ._2Y(n1_bit_multiplier_block_13_p2),
    .NEG(n1_bit_multiplier_block_13_p1));
  PPG ppg_77 (
    .PP(ppg_77_pp), .Yi(Yi_6), .Yi_1(Yi_1_6), .Y(booth_encoder_6_one), ._2Y(booth_encoder_6_two),
    .NEG(booth_encoder_6_neg));
  PPG ppg_78 (
    .PP(ppg_78_pp), .Yi(Yi_7), .Yi_1(Yi_1_7), .Y(booth_encoder_7_one), ._2Y(booth_encoder_7_two),
    .NEG(booth_encoder_7_neg));
  _1_bit_multiplier_block u_1_bit_multiplier_block_81 ();  // open: PP, Sin, en, Cin, out_6, out_5
  PPG ppg_79 (.PP(ppg_79_pp), .Yi(Yi), .Yi_1(Yi), .Y(Yi), ._2Y(Yi), .NEG(Yi));
  PPG ppg_80 (
    .PP(ppg_80_pp), .Yi(Yi_2), .Yi_1(Yi_1_2), .Y(booth_encoder_2_one), ._2Y(booth_encoder_2_two),
    .NEG(booth_encoder_2_neg));
  _1_bit_multiplier_block u_1_bit_multiplier_block_82 (
    .PP(ppg_80_pp), .en(control_circuit_1_out_7), .Cin(n1_bit_multiplier_block_88_out_6),
    .out_6(n1_bit_multiplier_block_82_out_6));  // open: Sin, out_5
  PPG ppg_81 (
    .PP(ppg_81_pp), .Yi(Yi_3), .Yi_1(Yi_1_3), .Y(n1_bit_multiplier_block_29_p5),
    ._2Y(n1_bit_multiplier_block_29_p4), .NEG(n1_bit_multiplier_block_29_p3));
  _1_bit_multiplier_block u_1_bit_multiplier_block_83 (
    .PP(ppg_81_pp), .Cin(n1_bit_multiplier_block_89_out_6), .out_6(n1_bit_multiplier_block_83_out_6),
    .out_5(n1_bit_multiplier_block_83_out_5));  // open: Sin, en
  PPG ppg_82 (
    .PP(ppg_82_pp), .Yi(Yi_4), .Yi_1(Yi_1_4), .Y(n1_bit_multiplier_block_22_p3),
    ._2Y(n1_bit_multiplier_block_22_p2), .NEG(n1_bit_multiplier_block_22_p1));
  _1_bit_multiplier_block u_1_bit_multiplier_block_84 (
    .PP(ppg_82_pp), .Sin(n1_bit_multiplier_block_83_out_5), .Cin(n1_bit_multiplier_block_90_out_6),
    .out_6(n1_bit_multiplier_block_84_out_6), .out_5(n1_bit_multiplier_block_84_out_5));  // open: en
  PPG ppg_83 (
    .PP(ppg_83_pp), .Yi(Yi_5), .Yi_1(Yi_1_5), .Y(in_28), ._2Y(n1_bit_multiplier_block_13_p2),
    .NEG(n1_bit_multiplier_block_13_p1));
  _1_bit_multiplier_block u_1_bit_multiplier_block_85 (
    .PP(ppg_83_pp), .Sin(n1_bit_multiplier_block_84_out_5), .Cin(n1_bit_multiplier_block_91_out_6),
    .out_6(n1_bit_multiplier_block_85_out_6));  // open: en, out_5
  PPG ppg_84 (
    .PP(ppg_84_pp), .Yi(Yi_6), .Yi_1(Yi_1_6), .Y(booth_encoder_6_one), ._2Y(booth_encoder_6_two),
    .NEG(booth_encoder_6_neg));
  _1_bit_multiplier_block u_1_bit_multiplier_block_86 (
    .PP(ppg_84_pp), .Cin(n1_bit_multiplier_block_92_out_6), .out_6(n1_bit_multiplier_block_86_out_6),
    .out_5(n1_bit_multiplier_block_86_out_5));  // open: Sin, en
  PPG ppg_85 (.PP(control_circuit_1_out_7), .Yi(Yi), .Yi_1(Yi), .Y(Yi), ._2Y(Yi), .NEG(Yi));
  _1_bit_multiplier_block u_1_bit_multiplier_block_87 (
    .PP(control_circuit_1_out_7), .en(control_circuit_1_out_7), .Cin(control_circuit_1_out_7),
    .out_6(n1_bit_multiplier_block_87_out_6));  // open: Sin, out_5
  _1_bit_multiplier_block u_1_bit_multiplier_block_88 (
    .PP(control_circuit_1_out_7), .en(control_circuit_1_out_7), .Cin(n1_bit_multiplier_block_94_out_6),
    .out_6(n1_bit_multiplier_block_88_out_6));  // open: Sin, out_5
  _1_bit_multiplier_block u_1_bit_multiplier_block_89 (
    .PP(ppg_88_pp), .Cin(n1_bit_multiplier_block_95_out_6), .out_6(n1_bit_multiplier_block_89_out_6),
    .out_5(n1_bit_multiplier_block_89_out_5));  // open: Sin, en
  PPG ppg_86 (
    .PP(ppg_86_pp), .Yi(Yi_4), .Yi_1(Yi_1_4), .Y(n1_bit_multiplier_block_22_p3),
    ._2Y(n1_bit_multiplier_block_22_p2), .NEG(n1_bit_multiplier_block_22_p1));
  _1_bit_multiplier_block u_1_bit_multiplier_block_90 (
    .PP(ppg_86_pp), .Sin(n1_bit_multiplier_block_89_out_5), .Cin(n1_bit_multiplier_block_96_out_6),
    .out_6(n1_bit_multiplier_block_90_out_6), .out_5(n1_bit_multiplier_block_90_out_5));  // open: en
  _1_bit_multiplier_block u_1_bit_multiplier_block_91 (
    .PP(ppg_89_pp), .Sin(n1_bit_multiplier_block_90_out_5), .Cin(n1_bit_multiplier_block_97_out_6),
    .out_6(n1_bit_multiplier_block_91_out_6));  // open: en, out_5
  _1_bit_multiplier_block u_1_bit_multiplier_block_92 (
    .PP(ppg_90_pp), .out_6(n1_bit_multiplier_block_92_out_6), .out_5(n1_bit_multiplier_block_92_out_5));  // open: Sin, en, Cin
  _1_bit_multiplier_block u_1_bit_multiplier_block_93 (
    .PP(ppg_91_pp), .en(control_circuit_1_out_7), .Cin(n1_bit_multiplier_block_98_out_6),
    .out_6(control_circuit_1_out_7));  // open: Sin, out_5
  PPG ppg_87 (
    .PP(control_circuit_1_out_7), .Yi(Yi_2), .Yi_1(Yi_1_2), .Y(booth_encoder_2_one),
    ._2Y(booth_encoder_2_two), .NEG(booth_encoder_2_neg));
  _1_bit_multiplier_block u_1_bit_multiplier_block_94 (
    .PP(ppg_92_pp), .en(control_circuit_1_out_6), .Cin(n1_bit_multiplier_block_99_out_6),
    .out_6(n1_bit_multiplier_block_94_out_6));  // open: Sin, out_5
  PPG ppg_88 (
    .PP(ppg_88_pp), .Yi(Yi_3), .Yi_1(Yi_1_3), .Y(n1_bit_multiplier_block_29_p5),
    ._2Y(n1_bit_multiplier_block_29_p4), .NEG(n1_bit_multiplier_block_29_p3));
  _1_bit_multiplier_block u_1_bit_multiplier_block_95 (
    .PP(ppg_93_pp), .en(undriven), .Cin(n1_bit_multiplier_block_100_out_6),
    .out_6(n1_bit_multiplier_block_95_out_6), .out_5(n1_bit_multiplier_block_95_out_5));  // open: Sin
  _1_bit_multiplier_block u_1_bit_multiplier_block_96 (
    .PP(ppg_94_pp), .Sin(n1_bit_multiplier_block_95_out_5), .Cin(n1_bit_multiplier_block_101_out_6),
    .out_6(n1_bit_multiplier_block_96_out_6), .out_5(n1_bit_multiplier_block_96_out_5));  // open: en
  PPG ppg_89 (
    .PP(ppg_89_pp), .Yi(Yi_5), .Yi_1(Yi_1_5), .Y(in_28), ._2Y(n1_bit_multiplier_block_13_p2),
    .NEG(n1_bit_multiplier_block_13_p1));
  _1_bit_multiplier_block u_1_bit_multiplier_block_97 (
    .PP(ppg_95_pp), .Sin(n1_bit_multiplier_block_96_out_5), .Cin(n1_bit_multiplier_block_102_out_6),
    .out_6(n1_bit_multiplier_block_97_out_6), .out_5(n1_bit_multiplier_block_97_out_5));  // open: en
  PPG ppg_90 (
    .PP(ppg_90_pp), .Yi(Yi_6), .Yi_1(Yi_1_6), .Y(booth_encoder_6_one), ._2Y(booth_encoder_6_two),
    .NEG(booth_encoder_6_neg));
  PPG ppg_91 (.PP(ppg_91_pp), .Yi(Yi), .Yi_1(Yi), .Y(Yi), ._2Y(Yi), .NEG(Yi));
  _1_bit_multiplier_block u_1_bit_multiplier_block_98 (
    .PP(ppg_96_pp), .en(control_circuit_1_out_7), .Cin(n1_bit_multiplier_block_103_out_6),
    .out_6(n1_bit_multiplier_block_98_out_6));  // open: Sin, out_5
  PPG ppg_92 (
    .PP(ppg_92_pp), .Yi(Yi_2), .Yi_1(Yi_1_2), .Y(booth_encoder_2_one), ._2Y(booth_encoder_2_two),
    .NEG(booth_encoder_2_neg));
  _1_bit_multiplier_block u_1_bit_multiplier_block_99 (
    .PP(ppg_97_pp), .en(control_circuit_1_out_6), .Cin(n1_bit_multiplier_block_104_out_6),
    .out_6(n1_bit_multiplier_block_99_out_6));  // open: Sin, out_5
  PPG ppg_93 (
    .PP(ppg_93_pp), .Yi(Yi_3), .Yi_1(Yi_1_3), .Y(n1_bit_multiplier_block_29_p5),
    ._2Y(n1_bit_multiplier_block_29_p4), .NEG(n1_bit_multiplier_block_29_p3));
  _1_bit_multiplier_block u_1_bit_multiplier_block_100 (
    .PP(ppg_98_pp), .en(undriven_2), .Cin(n1_bit_multiplier_block_105_out_6),
    .out_6(n1_bit_multiplier_block_100_out_6), .out_5(n1_bit_multiplier_block_100_out_5));  // open: Sin
  PPG ppg_94 (
    .PP(ppg_94_pp), .Yi(Yi_4), .Yi_1(Yi_1_4), .Y(n1_bit_multiplier_block_22_p3),
    ._2Y(n1_bit_multiplier_block_22_p2), .NEG(n1_bit_multiplier_block_22_p1));
  _1_bit_multiplier_block u_1_bit_multiplier_block_101 (
    .PP(ppg_99_pp), .Sin(n1_bit_multiplier_block_100_out_5), .Cin(n1_bit_multiplier_block_106_out_6),
    .out_6(n1_bit_multiplier_block_101_out_6), .out_5(n1_bit_multiplier_block_101_out_5));  // open: en
  PPG ppg_95 (
    .PP(ppg_95_pp), .Yi(Yi_5), .Yi_1(Yi_1_5), .Y(in_28), ._2Y(n1_bit_multiplier_block_13_p2),
    .NEG(n1_bit_multiplier_block_13_p1));
  _1_bit_multiplier_block u_1_bit_multiplier_block_102 (
    .PP(ppg_100_pp), .Sin(n1_bit_multiplier_block_101_out_5), .out_6(n1_bit_multiplier_block_102_out_6),
    .out_5(n1_bit_multiplier_block_102_out_5));  // open: en, Cin
  PPG ppg_96 (.PP(ppg_96_pp), .Yi(Yi), .Yi_1(Yi), .Y(Yi), ._2Y(Yi), .NEG(Yi));
  PPG ppg_97 (
    .PP(ppg_97_pp), .Yi(Yi_2), .Yi_1(Yi_1_2), .Y(booth_encoder_2_one), ._2Y(booth_encoder_2_two),
    .NEG(booth_encoder_2_neg));
  PPG ppg_98 (
    .PP(ppg_98_pp), .Yi(Yi_3), .Yi_1(Yi_1_3), .Y(n1_bit_multiplier_block_29_p5),
    ._2Y(n1_bit_multiplier_block_29_p3), .NEG(n1_bit_multiplier_block_29_p3));
  PPG ppg_99 (
    .PP(ppg_99_pp), .Yi(Yi_4), .Yi_1(Yi_1_4), .Y(n1_bit_multiplier_block_22_p3),
    ._2Y(n1_bit_multiplier_block_22_p2), .NEG(n1_bit_multiplier_block_22_p1));
  PPG ppg_100 (
    .PP(ppg_100_pp), .Yi(Yi_5), .Yi_1(Yi_1_5), .Y(in_28), ._2Y(n1_bit_multiplier_block_13_p2),
    .NEG(n1_bit_multiplier_block_13_p1));
  PPG ppg_101 (.PP(control_circuit_1_out_6), .Yi(Yi), .Yi_1(Yi), .Y(Yi), ._2Y(Yi), .NEG(Yi));
  _1_bit_multiplier_block u_1_bit_multiplier_block_103 (
    .PP(control_circuit_1_out_6), .en(control_circuit_1_out_6), .out_6(n1_bit_multiplier_block_103_out_6));  // open: Sin, Cin, out_5
  PPG ppg_102 (
    .PP(ppg_102_pp), .Yi(Yi_2), .Yi_1(Yi_1_2), .Y(booth_encoder_2_one), ._2Y(booth_encoder_2_two),
    .NEG(booth_encoder_2_neg));
  _1_bit_multiplier_block u_1_bit_multiplier_block_104 (
    .PP(ppg_102_pp), .en(control_circuit_1_out_6), .Cin(n1_bit_multiplier_block_109_out_6),
    .out_6(n1_bit_multiplier_block_104_out_6));  // open: Sin, out_5
  PPG ppg_103 (
    .PP(ppg_103_pp), .Yi(Yi_3), .Yi_1(Yi_1_3), .Y(n1_bit_multiplier_block_29_p5),
    ._2Y(n1_bit_multiplier_block_29_p4), .NEG(n1_bit_multiplier_block_29_p3));
  _1_bit_multiplier_block u_1_bit_multiplier_block_105 (
    .PP(ppg_103_pp), .en(undriven_3), .Cin(n1_bit_multiplier_block_110_out_6),
    .out_6(n1_bit_multiplier_block_105_out_6), .out_5(n1_bit_multiplier_block_105_out_5));  // open: Sin
  PPG ppg_104 (
    .PP(ppg_104_pp), .Yi(Yi_4), .Yi_1(Yi_1_4), .Y(n1_bit_multiplier_block_22_p3),
    ._2Y(n1_bit_multiplier_block_22_p2), .NEG(n1_bit_multiplier_block_22_p1));
  _1_bit_multiplier_block u_1_bit_multiplier_block_106 (
    .PP(ppg_104_pp), .Sin(n1_bit_multiplier_block_105_out_5), .Cin(n1_bit_multiplier_block_111_out_6),
    .out_6(n1_bit_multiplier_block_106_out_6), .out_5(n1_bit_multiplier_block_106_out_5));  // open: en
  _1_bit_multiplier_block u_1_bit_multiplier_block_107 ();  // open: PP, Sin, en, Cin, out_6, out_5
  _1_bit_multiplier_block u_1_bit_multiplier_block_108 (
    .PP(ppg_106_pp), .en(control_circuit_1_out_6), .Cin(n1_bit_multiplier_block_112_out_6));  // open: Sin, out_6, out_5
  PPG ppg_105 (
    .PP(ppg_105_pp), .Yi(Yi_2), .Yi_1(Yi_1_2), .Y(booth_encoder_2_one), ._2Y(booth_encoder_2_two),
    .NEG(booth_encoder_2_neg));
  _1_bit_multiplier_block u_1_bit_multiplier_block_109 (
    .PP(ppg_105_pp), .en(undriven_4), .Cin(n1_bit_multiplier_block_113_out_6),
    .out_6(n1_bit_multiplier_block_109_out_6));  // open: Sin, out_5
  _1_bit_multiplier_block u_1_bit_multiplier_block_110 (
    .en(Yi), .Cin(n1_bit_multiplier_block_114_out_6), .out_6(n1_bit_multiplier_block_110_out_6),
    .out_5(n1_bit_multiplier_block_110_out_5));  // open: PP, Sin
  _1_bit_multiplier_block u_1_bit_multiplier_block_111 (
    .PP(ppg_108_pp), .Sin(n1_bit_multiplier_block_110_out_5), .out_6(n1_bit_multiplier_block_111_out_6),
    .out_5(n1_bit_multiplier_block_111_out_5));  // open: en, Cin
  PPG ppg_106 (.PP(ppg_106_pp), .Yi(Yi), .Yi_1(Yi), .Y(Yi), ._2Y(Yi), .NEG(Yi));
  _1_bit_multiplier_block u_1_bit_multiplier_block_112 (
    .PP(ppg_109_pp), .en(control_circuit_1_out_6), .Cin(n1_bit_multiplier_block_115_out_6),
    .out_6(n1_bit_multiplier_block_112_out_6));  // open: Sin, out_5
  _1_bit_multiplier_block u_1_bit_multiplier_block_113 (
    .PP(ppg_110_pp), .en(control_circuit_1_out_5), .Cin(n1_bit_multiplier_block_116_out_6),
    .out_6(n1_bit_multiplier_block_113_out_6));  // open: Sin, out_5
  PPG ppg_107 (
    .Yi(Yi_3), .Yi_1(Yi_1_3), .Y(n1_bit_multiplier_block_29_p5), ._2Y(n1_bit_multiplier_block_29_p4),
    .NEG(n1_bit_multiplier_block_29_p3));  // open: PP
  _1_bit_multiplier_block u_1_bit_multiplier_block_114 (
    .PP(ppg_111_pp), .en(Yi), .Cin(n1_bit_multiplier_block_117_out_6),
    .out_6(n1_bit_multiplier_block_114_out_6), .out_5(n1_bit_multiplier_block_114_out_5));  // open: Sin
  PPG ppg_108 (
    .PP(ppg_108_pp), .Yi(Yi_4), .Yi_1(Yi_1_4), .Y(n1_bit_multiplier_block_22_p3),
    ._2Y(n1_bit_multiplier_block_22_p2), .NEG(n1_bit_multiplier_block_22_p1));
  PPG ppg_109 (.PP(ppg_109_pp), .Yi(Yi), .Yi_1(Yi), .Y(Yi), ._2Y(Yi), .NEG(Yi));
  _1_bit_multiplier_block u_1_bit_multiplier_block_115 (
    .PP(ppg_112_pp), .en(control_circuit_1_out_6), .Cin(n1_bit_multiplier_block_118_out_6),
    .out_6(n1_bit_multiplier_block_115_out_6));  // open: Sin, out_5
  PPG ppg_110 (
    .PP(ppg_110_pp), .Yi(Yi_2), .Yi_1(Yi_1_2), .Y(booth_encoder_2_one), ._2Y(booth_encoder_2_two),
    .NEG(booth_encoder_2_neg));
  _1_bit_multiplier_block u_1_bit_multiplier_block_116 (
    .PP(ppg_113_pp), .en(control_circuit_1_out_5), .Cin(n1_bit_multiplier_block_119_out_6),
    .out_6(n1_bit_multiplier_block_116_out_6), .out_5(n1_bit_multiplier_block_29_p5));  // open: Sin
  PPG ppg_111 (
    .PP(ppg_111_pp), .Yi(Yi_3), .Yi_1(Yi_1_3), .Y(n1_bit_multiplier_block_29_p5),
    ._2Y(n1_bit_multiplier_block_29_p4), .NEG(n1_bit_multiplier_block_29_p3));
  _1_bit_multiplier_block u_1_bit_multiplier_block_117 (
    .PP(ppg_114_pp), .en(Yi), .out_6(n1_bit_multiplier_block_117_out_6),
    .out_5(n1_bit_multiplier_block_117_out_5));  // open: Sin, Cin
  PPG ppg_112 (.PP(ppg_112_pp), .Yi(Yi), .Yi_1(Yi), .Y(Yi), ._2Y(Yi), .NEG(Yi));
  PPG ppg_113 (
    .PP(ppg_113_pp), .Yi(Yi_2), .Yi_1(Yi_1_2), .Y(booth_encoder_2_one), ._2Y(booth_encoder_2_neg),
    .NEG(booth_encoder_2_neg));
  PPG ppg_114 (
    .PP(ppg_114_pp), .Yi(Yi_3), .Yi_1(Yi_1_3), .Y(n1_bit_multiplier_block_29_p5),
    ._2Y(n1_bit_multiplier_block_29_p4), .NEG(n1_bit_multiplier_block_29_p3));
  PPG ppg_115 (.PP(ppg_115_pp), .Yi(Yi), .Yi_1(Yi), .Y(Yi), ._2Y(Yi), .NEG(Yi));
  _1_bit_multiplier_block u_1_bit_multiplier_block_118 (
    .PP(ppg_115_pp), .en(control_circuit_1_out_5), .Cin(n1_bit_multiplier_block_120_out_6),
    .out_6(n1_bit_multiplier_block_118_out_6));  // open: Sin, out_5
  PPG ppg_116 (
    .PP(ppg_116_pp), .Yi(Yi_2), .Yi_1(Yi_1_2), .Y(booth_encoder_2_one), ._2Y(booth_encoder_2_two),
    .NEG(booth_encoder_2_neg));
  _1_bit_multiplier_block u_1_bit_multiplier_block_119 (
    .PP(ppg_116_pp), .en(control_circuit_1_out_5), .Cin(control_circuit_1_out_5),
    .out_6(n1_bit_multiplier_block_119_out_6), .out_5(n1_bit_multiplier_block_119_out_5));  // open: Sin
  _1_bit_multiplier_block u_1_bit_multiplier_block_120 (
    .PP(ppg_117_pp), .en(control_circuit_1_out_5), .Cin(n1_bit_multiplier_block_122_out_6),
    .out_6(n1_bit_multiplier_block_120_out_6), .out_5(n1_bit_multiplier_block_120_out_5));  // open: Sin
  _1_bit_multiplier_block u_1_bit_multiplier_block_121 (
    .PP(ppg_118_pp), .Sin(n1_bit_multiplier_block_120_out_5), .en(control_circuit_1_out_5),
    .out_6(control_circuit_1_out_5), .out_5(n1_bit_multiplier_block_121_out_5));  // open: Cin
  PPG ppg_117 (.PP(ppg_117_pp), .Yi(Yi), .Yi_1(Yi), .Y(Yi), ._2Y(Yi), .NEG(Yi));
  _1_bit_multiplier_block u_1_bit_multiplier_block_122 (
    .PP(ppg_119_pp), .en(control_circuit_1_out_5), .Cin(n1_bit_multiplier_block_123_out_6),
    .out_6(n1_bit_multiplier_block_122_out_6), .out_5(n1_bit_multiplier_block_122_out_5));  // open: Sin
  PPG ppg_118 (
    .PP(ppg_118_pp), .Yi(Yi_2), .Yi_1(Yi_1_2), .Y(booth_encoder_2_one), ._2Y(booth_encoder_2_two),
    .NEG(booth_encoder_2_neg));
  PPG ppg_119 (.PP(ppg_119_pp), .Yi(Yi), .Yi_1(Yi), .Y(Yi), ._2Y(Yi), .NEG(Yi));
  _1_bit_multiplier_block u_1_bit_multiplier_block_123 (
    .PP(ppg_120_pp), .en(control_circuit_1_out_5), .out_6(n1_bit_multiplier_block_123_out_6),
    .out_5(n1_bit_multiplier_block_123_out_5));  // open: Sin, Cin
  PPG ppg_120 (.PP(ppg_120_pp), .Yi(Yi), .Yi_1(Yi), .Y(Yi), ._2Y(Yi), .NEG(Yi));
  Booth_Encoder booth_encoder_1 (.NEG(Yi), .TWO(Yi), .ONE(Yi), .qi_1(Multiplier_Bits), .qi(in_6), .qi_1_2(in_7));
  Booth_Encoder booth_encoder_2 (
    .NEG(booth_encoder_2_neg), .TWO(booth_encoder_2_two), .ONE(booth_encoder_2_one), .qi_1(in_11),
    .qi(in_12), .qi_1_2(in_13));
  Booth_Encoder booth_encoder_3 (
    .NEG(n1_bit_multiplier_block_29_p3), .TWO(n1_bit_multiplier_block_29_p4),
    .ONE(n1_bit_multiplier_block_29_p5), .qi_1(in_16), .qi(in_17), .qi_1_2(in_18));
  Booth_Encoder booth_encoder_4 (
    .NEG(n1_bit_multiplier_block_22_p1), .TWO(n1_bit_multiplier_block_22_p2),
    .ONE(n1_bit_multiplier_block_22_p3), .qi_1(in_21), .qi(in_22), .qi_1_2(in_23));
  Booth_Encoder booth_encoder_5 (
    .NEG(n1_bit_multiplier_block_13_p1), .TWO(n1_bit_multiplier_block_13_p2), .ONE(in_28), .qi_1(in_26),
    .qi(in_27), .qi_1_2(in_28));
  Booth_Encoder booth_encoder_6 (
    .NEG(booth_encoder_6_neg), .TWO(booth_encoder_6_two), .ONE(booth_encoder_6_one), .qi_1(in_31),
    .qi(in_32), .qi_1_2(in_33));
  Booth_Encoder booth_encoder_7 (
    .NEG(booth_encoder_7_neg), .TWO(booth_encoder_7_two), .ONE(booth_encoder_7_one), .qi_1(in_36),
    .qi(in_37), .qi_1_2(in_38));
  Booth_Encoder booth_encoder_8 (
    .NEG(booth_encoder_8_neg), .TWO(booth_encoder_8_two), .ONE(booth_encoder_8_one), .qi_1(in_41),
    .qi(in_42), .qi_1_2(in_43));

  assign Yi_1 = Yi;
endmodule

module PPG (
  input  Yi,
  input  Yi_1,
  input  Y,
  input  _2Y,
  input  NEG,
  output PP
);

  wire nand_1_out, nand_2_out, nand_3_out;

  xor xor_1 (PP, nand_1_out, NEG);
  nand nand_1 (nand_1_out, nand_2_out, nand_3_out);
  nand nand_2 (nand_2_out, Yi, Y);
  nand nand_3 (nand_3_out, Yi_1, _2Y);
endmodule

// Encoder
module Booth_Encoder (
  input  qi_1,
  input  qi,
  input  qi_1_2,
  output NEG,
  output TWO,
  output ONE
);

  wire and_1_out, and_2_out, not_1_out, not_2_out;

  Multiplexer #(.enable("false")) multiplexer_1 (.in0(and_1_out), .in1(and_2_out), .out(TWO), .sel(qi_1));
  and and_1 (and_1_out, qi, qi_1_2);
  and and_2 (and_2_out, not_1_out, not_2_out);
  not not_1 (not_1_out, qi);
  not not_2 (not_2_out, qi_1_2);
  xor xor_1 (ONE, qi, qi_1_2);
  // NOT_Gate not_3 is placed but not wired

  assign NEG = qi_1;
endmodule

// multiplier
module _1_bit_multiplier_block (
  input  Cin,
  input  PP,
  input  Sin,
  input  en,
  output out_5,
  output out_6
);

  wire and_1_out;

  and and_1 (and_1_out, Sin, en);
  Adder #(.width(1)) adder_1 (.a(PP), .b(and_1_out), .out(out_5), .cin(Cin), .cout(out_6));
endmodule

// control unit
module control_circuit (
  input  ctlA_0,
  input  ctlA_1,
  input  ctlB_0,
  input  ctlB_1,
  output out_5,
  output out_6,
  output out_7,
  output out_8,
  output out_9,
  output out_10,
  output out_11,
  output out_12,
  output out_13,
  output out_14,
  output out_15,
  output out_16,
  output out_17,
  output out_18,
  output out_19,
  output out_20
);

  and and_1 (out_17, ctlA_0, ctlA_1);
  or or_1 (out_19, ctlA_0, ctlA_1);
  and and_2 (out_8, ctlB_0, ctlB_1);
  or or_2 (out_16, ctlB_0, ctlB_1);
  and and_3 (out_11, ctlB_1, out_19);
  and and_4 (out_10, ctlB_1, ctlA_1);
  and and_5 (out_7, ctlB_1, out_17);
  and and_6 (out_13, out_17, out_16);
  and and_7 (out_14, ctlA_1, out_16);
  and and_8 (out_15, out_19, out_16);
  and and_9 (out_5, out_8, out_17);
  and and_10 (out_6, out_8, ctlA_1);
  and and_11 (out_7, out_8, out_19);

  assign out_9 = out_7;
  assign out_12 = ctlB_1;
  assign out_18 = ctlA_1;
  assign out_20 = 1'b1;

  // Notes on the sheet:
  //   RV1_en
  //   RV2_en
  //   RV3_en
  //   RH1_en
  //   RH2_en
  //   RH3_en
endmodule
